// Logisim project ALU.circ as structural Verilog: 1 circuit, main circuit ALU
module ALU (
  input  [31:0] A,
  input  [31:0] B,
  input  [4:0] Shift,
  input  [3:0] Codop,
  input  CarryIn,
  output [31:0] S,
  output [3:0] Flags
);

  wire adder_1_cout, adder_2_cout, and_4_out, and_5_out, and_6_out, and_7_out, and_8_out, bitselector_2_out,
       bitselector_3_out, bitselector_4_out, bitselector_5_out, bitselector_6_out, bitselector_7_out,
       bitselector_8_out, bitselector_11_out, bitselector_12_out, bitselector_13_out, bitselector_14_out,
       bitselector_15_out, bitselector_16_out, bitselector_17_out, c1, c2, comparator_1_eq, comparator_2_eq,
       comparator_3_eq, comparator_4_eq, comparator_5_eq, comparator_6_eq, comparator_7_eq, comparator_8_eq,
       comparator_9_eq, comparator_10_eq, Dernier, not_1_out, not_4_out, not_5_out, subtractor_1_bout,
       subtractor_3_bout;
  wire [4:0] subtractor_4_out, subtractor_5_out;
  wire [31:0] adder_1_out, adder_2_out, and_1_out, and_2_out, and_3_out, multiplier_1_out, not_2_out,
       not_3_out, or_1_out, rsb, shifter_1_out, shifter_2_out, shifter_3_out, shifter_4_out,
       subtractor_1_out, subtractor_3_out, xnor_1_out, xnor_2_out, xor_1_out, xor_2_out, xor_3_out,
       xor_4_out, xor_5_out, xor_6_out, xor_7_out, xor_8_out, xor_9_out;

  not not_1 (not_1_out, CarryIn);
  assign not_2_out = ~A;  // NOT_Gate not_2, 32 bits wide
  assign and_1_out = A & B;  // AND_Gate and_1, 32 bits wide
  assign xor_1_out = A ^ B;  // XOR_Gate xor_1, 32 bits wide
  Shifter #(.width(32)) shifter_1 (.in(B), .\dist (Shift), .out(shifter_1_out));
  Shifter #(.shift("lr"), .width(32)) shifter_2 (.in(B), .\dist (Shift), .out(shifter_2_out));
  Shifter #(.shift("ar"), .width(32)) shifter_3 (.in(B), .\dist (Shift), .out(shifter_3_out));
  Adder #(.width(32)) adder_1 (.a(A), .b(B), .out(adder_1_out), .cin(CarryIn), .cout(adder_1_cout));
  Subtractor #(.width(32)) subtractor_1 (
    .a(B), .b(A), .out(subtractor_1_out), .bin(not_1_out), .bout(subtractor_1_bout));
  Shifter #(.shift("rr"), .width(32)) shifter_4 (.in(B), .\dist (Shift), .out(shifter_4_out));
  Subtractor #(.width(32)) subtractor_2 (.a({32{1'b0}}), .b(A), .out(rsb));  // open: bin, bout
  Subtractor #(.width(32)) subtractor_3 (.a(B), .b(A), .out(subtractor_3_out), .bout(subtractor_3_bout));  // open: bin
  Adder #(.width(32)) adder_2 (.a(A), .b(B), .out(adder_2_out), .cout(adder_2_cout));  // open: cin
  assign or_1_out = A | B;  // OR_Gate or_1, 32 bits wide
  Multiplier #(.width(32)) multiplier_1 (.a(A), .b(B), .out(multiplier_1_out));  // open: cin, cout
  assign and_2_out = B & not_2_out;  // AND_Gate and_2, 32 bits wide
  assign not_3_out = ~A;  // NOT_Gate not_3, 32 bits wide
  not not_4 (not_4_out, subtractor_3_bout);
  Multiplexer #(.enable("false"), .select(4), .width(32)) multiplexer_1 (
    .in0(and_1_out), .in1(xor_1_out), .in2(shifter_1_out), .in3(shifter_2_out), .in4(shifter_3_out),
    .in5(adder_1_out), .in6(subtractor_1_out), .in7(shifter_4_out), .in8(B), .in9(rsb), .in10(B), .in11(B),
    .in12(or_1_out), .in13(multiplier_1_out), .in14(and_2_out), .in15(not_3_out), .out(S), .sel(Codop));
  not not_5 (not_5_out, subtractor_1_bout);
  BitSelector #(.width(32)) bitselector_1 (.in(S), .out(Dernier), .sel({5{1'b1}}));
  assign and_3_out = B & A;  // AND_Gate and_3, 32 bits wide
  BitSelector #(.width(32)) bitselector_2 (.in(xor_2_out), .out(bitselector_2_out), .sel({5{1'b1}}));
  assign xor_2_out = A ^ adder_1_out;  // XOR_Gate xor_2, 32 bits wide
  Multiplexer #(.enable("false"), .select(4)) multiplexer_2 (
    .in0(1'b0), .in1(1'b0), .in2(c1), .in3(c2), .in4(c2), .in5(adder_1_cout), .in6(not_5_out), .in7(Dernier),
    .in8(1'b0), .in9(1'b0), .in10(not_4_out), .in11(adder_2_cout), .in12(1'b0), .in13(1'b0), .in14(1'b0),
    .in15(1'b0), .out(Flags[1]), .sel(Codop));
  and and_4 (and_4_out, bitselector_2_out, bitselector_3_out);
  BitSelector #(.width(32)) bitselector_3 (.in(xnor_1_out), .out(bitselector_3_out), .sel({5{1'b1}}));
  assign xnor_1_out = ~(A ^ B);  // XNOR_Gate xnor_1, 32 bits wide
  and and_5 (and_5_out, bitselector_4_out, bitselector_5_out);
  BitSelector #(.width(32)) bitselector_4 (.in(xor_3_out), .out(bitselector_4_out), .sel({5{1'b1}}));
  BitSelector #(.width(32)) bitselector_5 (.in(xor_4_out), .out(bitselector_5_out), .sel({5{1'b1}}));
  assign xor_3_out = B ^ subtractor_1_out;  // XOR_Gate xor_3, 32 bits wide
  assign xor_4_out = B ^ A;  // XOR_Gate xor_4, 32 bits wide
  Subtractor #(.width(5)) subtractor_4 (.a({5{1'b0}}), .b(Shift), .out(subtractor_4_out));  // open: bin, bout
  Subtractor #(.width(5)) subtractor_5 (.a(Shift), .b(5'b00001), .out(subtractor_5_out));  // open: bin, bout
  and and_6 (and_6_out, bitselector_6_out, bitselector_7_out);
  BitSelector #(.width(32)) bitselector_6 (.in(xor_5_out), .out(bitselector_6_out), .sel({5{1'b1}}));
  BitSelector #(.width(32)) bitselector_7 (.in(xor_6_out), .out(bitselector_7_out), .sel({5{1'b1}}));
  assign xor_5_out = {32{1'b0}} ^ rsb;  // XOR_Gate xor_5, 32 bits wide
  assign xor_6_out = {32{1'b0}} ^ A;  // XOR_Gate xor_6, 32 bits wide
  BitSelector #(.width(32)) bitselector_8 (.in(rsb), .out(bitselector_8_out), .sel({5{1'b1}}));
  BitSelector #(.width(32)) bitselector_9 (.in(B), .out(c1), .sel(subtractor_4_out));
  BitSelector #(.width(32)) bitselector_10 (.in(B), .out(c2), .sel(subtractor_5_out));
  Multiplexer #(.enable("false"), .select(4)) multiplexer_3 (
    .in0(1'b0), .in1(1'b0), .in2(1'b0), .in3(1'b0), .in4(1'b0), .in5(and_4_out), .in6(and_5_out), .in7(1'b0),
    .in8(1'b0), .in9(and_6_out), .in10(and_7_out), .in11(and_8_out), .in12(1'b0), .in13(1'b0), .in14(1'b0),
    .in15(1'b0), .out(Flags[0]), .sel(Codop));
  and and_7 (and_7_out, bitselector_11_out, bitselector_12_out);
  BitSelector #(.width(32)) bitselector_11 (.in(xor_7_out), .out(bitselector_11_out), .sel({5{1'b1}}));
  assign xor_7_out = subtractor_3_out ^ B;  // XOR_Gate xor_7, 32 bits wide
  BitSelector #(.width(32)) bitselector_12 (.in(xor_8_out), .out(bitselector_12_out), .sel({5{1'b1}}));
  assign xor_8_out = B ^ A;  // XOR_Gate xor_8, 32 bits wide
  and and_8 (and_8_out, bitselector_13_out, bitselector_14_out);
  BitSelector #(.width(32)) bitselector_13 (.in(xor_9_out), .out(bitselector_13_out), .sel({5{1'b1}}));
  BitSelector #(.width(32)) bitselector_14 (.in(xnor_2_out), .out(bitselector_14_out), .sel({5{1'b1}}));
  assign xor_9_out = adder_2_out ^ A;  // XOR_Gate xor_9, 32 bits wide
  assign xnor_2_out = ~(A ^ B);  // XNOR_Gate xnor_2, 32 bits wide
  BitSelector #(.width(32)) bitselector_15 (.in(and_3_out), .out(bitselector_15_out), .sel({5{1'b1}}));
  BitSelector #(.width(32)) bitselector_16 (.in(subtractor_3_out), .out(bitselector_16_out), .sel({5{1'b1}}));
  BitSelector #(.width(32)) bitselector_17 (.in(adder_2_out), .out(bitselector_17_out), .sel({5{1'b1}}));
  Comparator #(.width(32)) comparator_1 (.a(rsb), .b({32{1'b0}}), .eq(comparator_1_eq));  // open: gt, lt
  Comparator #(.width(32)) comparator_2 (.a(and_3_out), .b({32{1'b0}}), .eq(comparator_2_eq));  // open: gt, lt
  Comparator #(.width(1)) comparator_3 (.a(bitselector_8_out), .b(1'b1), .eq(comparator_3_eq));  // open: gt, lt
  Comparator #(.width(1)) comparator_4 (.a(bitselector_15_out), .b(1'b1), .eq(comparator_4_eq));  // open: gt, lt
  Comparator #(.width(1)) comparator_5 (.a(bitselector_16_out), .b(1'b1), .eq(comparator_5_eq));  // open: gt, lt
  Comparator #(.width(1)) comparator_6 (.a(bitselector_17_out), .b(1'b1), .eq(comparator_6_eq));  // open: gt, lt
  Comparator #(.width(32)) comparator_7 (.a(adder_2_out), .b({32{1'b0}}), .eq(comparator_7_eq));  // open: gt, lt
  Comparator #(.width(32)) comparator_8 (.a(S), .b({32{1'b0}}), .eq(comparator_8_eq));  // open: gt, lt
  Comparator #(.width(32)) comparator_9 (.a(subtractor_3_out), .b({32{1'b0}}), .eq(comparator_9_eq));  // open: gt, lt
  Comparator #(.width(1)) comparator_10 (.a(Dernier), .b(1'b1), .eq(comparator_10_eq));  // open: gt, lt
  Multiplexer #(.enable("false"), .select(4)) multiplexer_4 (
    .in0(comparator_8_eq), .in1(comparator_8_eq), .in2(comparator_8_eq), .in3(comparator_8_eq),
    .in4(comparator_8_eq), .in5(comparator_8_eq), .in6(comparator_8_eq), .in7(comparator_8_eq),
    .in8(comparator_2_eq), .in9(comparator_1_eq), .in10(comparator_9_eq), .in11(comparator_7_eq),
    .in12(comparator_8_eq), .in13(comparator_8_eq), .in14(comparator_8_eq), .in15(comparator_8_eq),
    .out(Flags[2]), .sel(Codop));
  Multiplexer #(.enable("false"), .select(4)) multiplexer_5 (
    .in0(comparator_10_eq), .in1(comparator_10_eq), .in2(comparator_10_eq), .in3(comparator_10_eq),
    .in4(comparator_10_eq), .in5(comparator_10_eq), .in6(comparator_10_eq), .in7(comparator_10_eq),
    .in8(comparator_4_eq), .in9(comparator_3_eq), .in10(comparator_5_eq), .in11(comparator_6_eq),
    .in12(comparator_10_eq), .in13(comparator_10_eq), .in14(comparator_10_eq), .in15(comparator_10_eq),
    .out(Flags[3]), .sel(Codop));

  // Other names for the same wires on the sheet: codo[3:0] = Codop; decal[4:0] = Shift

  // Notes on the sheet:
  //   Note: for ROR, C = N
  //   Note 2: assume that shift > 0 for LSL and LSR
endmodule
