// Logisim project Ctl_Conditional.circ as structural Verilog: 1 circuit, main circuit Conditional
module Conditional (
  input  [15:0] Instruction,
  input  Enable,
  input  N,
  input  Z,
  input  C,
  input  V,
  output [10:0] Offset,
  output Verified
);

  wire and_1_out, and_2_out, and_3_out, and_4_out, and_5_out, and_6_out, and_7_out, and_8_out, and_9_out,
       and_10_out, and_11_out, and_12_out, and_13_out, and_14_out, and_15_out, and_16_out, GE, LT,
       multiplexer_3_out, or_1_out, or_2_out, or_3_out, S0, S1, S2, S3, S4, S5, S6, S7, S8, S9, S10, S11,
       S12, S13, S14;
  wire [10:0] bit_extender_1_out, multiplexer_1_out;

  Decoder #(.select(4)) decoder_1 (
    .out0(S0), .out1(S1), .out2(S2), .out3(S3), .out4(S4), .out5(S5), .out6(S6), .out7(S7), .out8(S8),
    .out9(S9), .out10(S10), .out11(S11), .out12(S12), .out13(S13), .out14(S14), .sel(Instruction[11:8]),
    .en(1'b1));  // open: out15
  assign bit_extender_1_out = {{3{Instruction[7]}}, Instruction[7:0]};  // Bit_Extender bit_extender_1
  xnor xnor_1 (LT, ~N, V);  // XNOR_Gate
  Multiplexer #(.enable("false"), .width(11)) multiplexer_1 (
    .in0(bit_extender_1_out), .in1(Instruction[10:0]), .out(multiplexer_1_out), .sel(Instruction[13]));
  xnor xnor_2 (GE, N, V);
  Multiplexer #(.enable("false"), .width(11)) multiplexer_2 (
    .in0({11{1'b0}}), .in1(multiplexer_1_out), .out(Offset), .sel(Verified));
  and and_1 (and_1_out, C, ~Z);  // AND_Gate
  or or_1 (or_1_out, ~C, Z);  // OR_Gate
  and and_2 (and_2_out, GE, S10);
  or or_2 (or_2_out, Z, LT);
  and and_3 (and_3_out, Z, S0);
  and and_4 (and_4_out, ~Z, S1);  // AND_Gate
  and and_5 (and_5_out, C, S2);
  and and_6 (and_6_out, ~C, S3);  // AND_Gate
  and and_7 (and_7_out, N, S4);
  and and_8 (and_8_out, ~N, S5);  // AND_Gate
  and and_9 (and_9_out, V, S6);
  and and_10 (and_10_out, ~V, S7);  // AND_Gate
  and and_11 (and_11_out, and_1_out, S8);
  and and_12 (and_12_out, or_1_out, S9);
  and and_13 (and_13_out, LT, S11);
  and and_14 (and_14_out, ~Z, GE);  // AND_Gate
  and and_15 (and_15_out, or_2_out, S13);
  or or_3 (or_3_out, multiplexer_3_out, Instruction[13]);
  Multiplexer #(.enable("false"), .select(4)) multiplexer_3 (
    .in0(and_3_out), .in1(and_4_out), .in2(and_5_out), .in3(and_6_out), .in4(and_7_out), .in5(and_8_out),
    .in6(and_9_out), .in7(and_10_out), .in8(and_11_out), .in9(and_12_out), .in10(and_2_out),
    .in11(and_13_out), .in12(and_16_out), .in13(and_15_out), .in14(1'b1), .out(multiplexer_3_out),
    .sel(Instruction[11:8]));  // open: in15
  and and_16 (and_16_out, and_14_out, S12);
  and and_17 (Verified, Enable, or_3_out);

  // Other names for the same wires on the sheet: B13 = Instruction[13]
endmodule
