// Logisim project Ctl_Data_Processing.circ as structural Verilog: 1 circuit, main circuit Data_Processing
module Data_Processing (
  input  [15:0] Instruction,
  input  Enable,
  output [2:0] Rd,
  output [2:0] Rn,
  output [2:0] Rm,
  output [3:0] ALU_Opcode,
  output [3:0] Flags_Update_Mask
);

  wire [2:0] five_to_three_pins;
  wire [3:0] bit_extender_2_out, multiplexer_1_out;
  wire [15:0] bit_extender_1_out;
  wire [15:10] and_1_out;

  assign bit_extender_1_out = {{15{Enable}}, Enable};  // Bit_Extender bit_extender_1
  assign {and_1_out, ALU_Opcode, five_to_three_pins, Rd} = Instruction & bit_extender_1_out;  // AND_Gate and_1, 16 bits wide
  assign bit_extender_2_out = {{3{Enable}}, Enable};  // Bit_Extender bit_extender_2
  Multiplexer #(.enable("false"), .select(4), .width(4)) multiplexer_1 (
    .in0(4'b1110), .in1(4'b1110), .in2(4'b1110), .in3(4'b1110), .in4(4'b1110), .in5(4'b1111), .in6(4'b1111),
    .in7(4'b1110), .in8(4'b1110), .in9(4'b1111), .in10(4'b1111), .in11(4'b1111), .in12(4'b1110),
    .in13(4'b1100), .in14(4'b1110), .in15(4'b1110), .out(multiplexer_1_out), .sel(ALU_Opcode));
  assign Flags_Update_Mask = multiplexer_1_out & bit_extender_2_out;  // AND_Gate and_2, 4 bits wide
  Multiplexer #(.enable("false"), .select(4), .width(3)) multiplexer_2 (
    .in0(five_to_three_pins), .in1(five_to_three_pins), .in2(five_to_three_pins), .in3(five_to_three_pins),
    .in4(five_to_three_pins), .in5(five_to_three_pins), .in6(five_to_three_pins), .in7(five_to_three_pins),
    .in8(five_to_three_pins), .in9(five_to_three_pins), .in10(five_to_three_pins), .in11(five_to_three_pins),
    .in12(five_to_three_pins), .in13(Rd), .in14(five_to_three_pins), .in15(five_to_three_pins), .out(Rm),
    .sel(ALU_Opcode));
  Multiplexer #(.enable("false"), .select(4), .width(3)) multiplexer_3 (
    .in0(Rd), .in1(Rd), .in2(Rd), .in3(Rd), .in4(Rd), .in5(Rd), .in6(Rd), .in7(Rd), .in8(Rd),
    .in9(five_to_three_pins), .in10(Rd), .in11(Rd), .in12(Rd), .in13(five_to_three_pins), .in14(Rd),
    .in15(Rd), .out(Rn), .sel(ALU_Opcode));

  // Other names for the same wires on the sheet: two_to_zero_pins[2:0] = Rd

  // Notes on the sheet:
  //   Note 2: RSB instruction has Rn as 1st operand.
  //   MUL instruction has Rn as 1st operand and Rdm as 2nd operand
  //   For simplification purposes, Rm is used for 1st operand both here and in the ALU.
  //   Note: instructions that does not save the result will still have the second operand as the destination register, the ALU will copy the second register to the destination register
  //   Pull output low on Enable = 0
endmodule
