// Logisim project Ctl_Load_Store.circ as structural Verilog: 1 circuit, main circuit Load_Store
module Load_Store (
  input  Enable,
  input  [15:0] Instruction,
  input  Clk,
  input  Reset,
  input  [31:0] Stack_Pointer,
  output Store,
  output Load,
  output PC_Hold,
  output [2:0] Rmd,
  output [31:0] RAM_Addr
);

  wire and_1_out, d_ff_1_q, d_ff_1_qn, not_1_out, not_2_out;
  wire [15:0] and_2_out, bit_extender_1_out;
  wire [31:0] bit_extender_3_out;

  assign bit_extender_1_out = {{15{Enable}}, Enable};  // Bit_Extender bit_extender_1
  Bit_Extender #(.in_width(1)) bit_extender_2 (.in(Enable));  // open: out
  and and_1 (and_1_out, d_ff_1_qn, Enable);
  assign {and_2_out[15:11], Rmd, and_2_out[7:0]} = Instruction & bit_extender_1_out;  // AND_Gate and_2, 16 bits wide
  D_Flip_Flop d_ff_1 (.D(and_1_out), .clk(Clk), .Q(d_ff_1_q), .Qn(d_ff_1_qn), .reset(Reset));  // open: preset
  assign bit_extender_3_out = {{24{and_2_out[7]}}, and_2_out[7:0]};  // Bit_Extender bit_extender_3
  and and_3 (Store, Enable, not_1_out);
  not not_1 (not_1_out, and_2_out[11]);
  and and_4 (Load, and_2_out[11], d_ff_1_q);
  not not_2 (not_2_out, d_ff_1_q);
  and and_5 (PC_Hold, not_2_out, Enable);
  Adder #(.width(32)) adder_1 (.a(bit_extender_3_out), .b(Stack_Pointer), .out(RAM_Addr));  // open: cin, cout

  // Notes on the sheet:
  //   Instruction: pull=down
  //   Delay load and hold PC for 1 cycle for the RAM to send out requested data 
endmodule
