// Logisim project Ctl_Shift_Add_Sub_Mov.circ as structural Verilog: 1 circuit, main circuit Shift_Add_Sub_Mov
module Shift_Add_Sub_Mov (
  input  Enable,
  input  [15:0] Instruction,
  output Carry,
  output Imm32_Enable,
  output [2:0] Rm,
  output [2:0] Rd,
  output [31:0] Imm32,
  output [3:0] Flags_Update_Mask,
  output [4:0] Imm5,
  output [2:0] Rn,
  output [3:0] ALU_Opcode
);

  wire add_i, add_r, and_2_out, and_3_out, and_4_out, and_5_out, and_6_out, and_7_out, and_8_out, and_9_out,
       and_10_out, and_11_out, and_12_out, and_13_out, and_14_out, and_15_out, i_AD, i_ADD, i_ASR, i_CMP,
       i_LSL, i_LSR, i_MOV, i_SUB, or_1_out, or_2_out, or_3_out, or_4_out, or_5_out, or_7_out, sub_i, sub_r;
  wire [2:0] imm31, multiplexer_6_out, multiplexer_9_out, Rd11, Rd21, Rd31, Rd41, Rdn51, Rm11, Rm21, Rn11,
       Rn21;
  wire [3:0] Code;
  wire [4:0] imm51;
  wire [7:0] imm81, negator_1_out;
  wire [15:0] and_17_out, and_18_out, bit_extender_1_out, bit_extender_2_out, bit_extender_3_out,
       bit_extender_4_out, bit_extender_5_out, bit_extender_6_out, insto;
  wire [15:9] and_19_out, and_20_out;
  wire [15:11] and_16_out;
  wire [31:0] bit_extender_7_out, bit_extender_8_out, bit_extender_9_out;

  assign bit_extender_1_out = {{15{Enable}}, Enable};  // Bit_Extender bit_extender_1
  Decoder #(.select(3)) decoder_1 (
    .out0(i_LSL), .out1(i_LSR), .out2(i_ASR), .out3(i_AD), .out4(i_MOV), .out5(i_CMP), .out6(i_ADD),
    .out7(i_SUB), .sel(insto[13:11]));  // open: en
  Decoder #(.select(2)) decoder_2 (
    .out0(add_r), .out1(sub_r), .out2(add_i), .out3(sub_i), .sel(insto[10:9]));  // open: en
  assign insto = Instruction & bit_extender_1_out;  // AND_Gate and_1, 16 bits wide
  and and_2 (and_2_out, ~Instruction[13], ~Instruction[12], ~Instruction[11]);  // AND_Gate
  and and_3 (and_3_out, ~Instruction[13], ~Instruction[12], Instruction[11]);  // AND_Gate
  and and_4 (and_4_out, ~Instruction[13], Instruction[12], Instruction[11], ~Instruction[10], ~Instruction[9]);  // AND_Gate
  and and_5 (and_5_out, ~Instruction[13], Instruction[12], Instruction[11], Instruction[10], ~Instruction[9]);  // AND_Gate
  and and_6 (and_6_out, Instruction[13], ~Instruction[12], ~Instruction[11]);  // AND_Gate
  and and_7 (and_7_out, Instruction[13], Instruction[12], ~Instruction[11]);  // AND_Gate
  and and_8 (and_8_out, ~Instruction[13], Instruction[12], ~Instruction[11]);  // AND_Gate
  and and_9 (and_9_out, ~Instruction[13], Instruction[12], Instruction[11], ~Instruction[10], Instruction[9]);  // AND_Gate
  and and_10 (and_10_out, ~Instruction[13], Instruction[12], Instruction[11], Instruction[10], Instruction[9]);  // AND_Gate
  and and_11 (and_11_out, Instruction[13], ~Instruction[12], Instruction[11]);  // AND_Gate
  and and_12 (and_12_out, Instruction[13], Instruction[12], Instruction[11]);
  Multiplexer #(.select(4), .width(3)) multiplexer_1 (
    .in0(Instruction[5:3]), .in1(Instruction[5:3]), .in2(Instruction[5:3]), .in3(Instruction[8:6]),
    .in4(Instruction[8:6]), .in5(3'b000), .in6(3'b000), .in7(3'b000), .in8(3'b000), .in9(3'b000),
    .in10(3'b000), .out(Rm), .sel(Code), .en(Enable));  // open: in11, in12, in13, in14, in15
  Priority_Encoder #(.select(4)) priority_encoder_1 (
    .in0(and_2_out), .in1(and_3_out), .in2(and_8_out), .in3(and_4_out), .in4(and_9_out), .in5(and_5_out),
    .in6(and_10_out), .in7(and_6_out), .in8(and_11_out), .in9(and_7_out), .in10(and_12_out), .out(Code));  // open: in11, in12, in13, in14, in15, gs, en_out, en_in
  Multiplexer #(.select(4), .width(4)) multiplexer_2 (
    .in0(4'b0010), .in1(4'b0011), .in2(4'b0100), .in3(4'b0101), .in4(4'b0110), .in5(4'b0101), .in6(4'b0110),
    .in7(4'b1001), .in8(4'b1010), .in9(4'b0101), .in10(4'b0110), .out(ALU_Opcode), .sel(Code), .en(Enable));  // open: in11, in12, in13, in14, in15
  Multiplexer #(.select(4), .width(4)) multiplexer_3 (
    .in0(4'b1110), .in1(4'b1110), .in2(4'b1110), .in3(4'b1111), .in4(4'b1111), .in5(4'b1111), .in6(4'b1111),
    .in7(4'b1100), .in8(4'b1111), .in9(4'b1111), .in10(4'b1111), .out(Flags_Update_Mask), .sel(Code),
    .en(Enable));  // open: in11, in12, in13, in14, in15
  Multiplexer #(.select(4), .width(5)) multiplexer_4 (
    .in0(Instruction[10:6]), .in1(Instruction[10:6]), .in2(Instruction[10:6]), .in3({5{1'b0}}),
    .in4({5{1'b0}}), .in5({5{1'b0}}), .in6({5{1'b0}}), .in7({5{1'b0}}), .in8({5{1'b0}}), .in9({5{1'b0}}),
    .in10({5{1'b0}}), .out(Imm5), .sel(Code), .en(Enable));  // open: in11, in12, in13, in14, in15
  or or_1 (or_1_out, i_LSL, i_LSR, i_ASR);
  or or_2 (or_2_out, add_r, sub_r);
  or or_3 (or_3_out, add_i, sub_i);
  or or_4 (or_4_out, i_MOV, i_CMP);
  or or_5 (or_5_out, i_ADD, i_SUB);
  Multiplexer #(.select(4)) multiplexer_5 (
    .in0(1'b0), .in1(1'b0), .in2(1'b0), .in3(1'b0), .in4(1'b0), .in5(1'b1), .in6(1'b1), .in7(1'b1),
    .in8(1'b1), .in9(1'b1), .in10(1'b1), .out(Imm32_Enable), .sel(Code), .en(Enable));  // open: in11, in12, in13, in14, in15
  assign Rd = Rd11 | Rd21 | Rd31 | Rd41 | Rdn51;  // OR_Gate or_6, 3 bits wide
  or or_7 (or_7_out, sub_i, sub_r);
  assign bit_extender_2_out = {{15{or_1_out}}, or_1_out};  // Bit_Extender bit_extender_2
  and and_13 (and_13_out, i_AD, or_2_out);
  and and_14 (and_14_out, i_AD, or_3_out);
  assign bit_extender_3_out = {{15{or_4_out}}, or_4_out};  // Bit_Extender bit_extender_3
  assign bit_extender_4_out = {{15{or_5_out}}, or_5_out};  // Bit_Extender bit_extender_4
  and and_15 (and_15_out, or_7_out, i_AD);
  assign {and_16_out, imm51, Rm11, Rd11} = bit_extender_2_out & insto;  // AND_Gate and_16, 16 bits wide
  assign bit_extender_5_out = {{15{and_13_out}}, and_13_out};  // Bit_Extender bit_extender_5
  assign bit_extender_6_out = {{15{and_14_out}}, and_14_out};  // Bit_Extender bit_extender_6
  assign {and_17_out[15:11], Rd41, and_17_out[7:0]} = bit_extender_3_out & insto;  // AND_Gate and_17, 16 bits wide
  assign {and_18_out[15:11], Rdn51, and_18_out[7:0]} = bit_extender_4_out & insto;  // AND_Gate and_18, 16 bits wide
  assign bit_extender_7_out = {{24{1'b0}}, Instruction[7:0]};  // Bit_Extender bit_extender_7
  assign bit_extender_8_out = {{24{1'b1}}, negator_1_out};  // Bit_Extender bit_extender_8
  Negator negator_1 (.in(Instruction[7:0]), .out(negator_1_out));
  or or_8 (Carry, and_15_out, i_SUB);
  assign {and_19_out, Rm21, Rn11, Rd21} = bit_extender_5_out & insto;  // AND_Gate and_19, 16 bits wide
  assign {and_20_out, imm31, Rn21, Rd31} = bit_extender_6_out & insto;  // AND_Gate and_20, 16 bits wide
  assign bit_extender_9_out = {{29{1'b0}}, Instruction[8:6]};  // Bit_Extender bit_extender_9
  Multiplexer #(.select(4), .width(3)) multiplexer_6 (
    .in0(Instruction[2:0]), .in1(Instruction[2:0]), .in2(Instruction[2:0]), .in3(Instruction[2:0]),
    .in4(Instruction[2:0]), .in5(Instruction[2:0]), .in6(Instruction[2:0]), .in7(Instruction[10:8]),
    .in8(Instruction[10:8]), .in9(Instruction[10:8]), .in10(Instruction[10:8]), .out(multiplexer_6_out),
    .sel(Code), .en(Enable));  // open: in11, in12, in13, in14, in15
  Multiplexer #(.select(4), .width(3)) multiplexer_7 (
    .in0(Instruction[5:3]), .in1(Instruction[5:3]), .in2(Instruction[5:3]), .in3(Instruction[5:3]),
    .in4(Instruction[5:3]), .in5(Instruction[5:3]), .in6(Instruction[5:3]), .in7(3'b000), .in8(3'b000),
    .in9(Instruction[10:8]), .in10(Instruction[10:8]), .out(Rn), .sel(Code), .en(Enable));  // open: in11, in12, in13, in14, in15
  Multiplexer #(.select(4), .width(32)) multiplexer_8 (
    .in0({32{1'b0}}), .in1({32{1'b0}}), .in2({32{1'b0}}), .in3({32{1'b0}}), .in4({32{1'b0}}),
    .in5(bit_extender_9_out), .in6(bit_extender_9_out), .in7(bit_extender_8_out), .in8(bit_extender_7_out),
    .in9(bit_extender_7_out), .in10(bit_extender_7_out), .out(Imm32), .sel(Code), .en(Enable));  // open: in11, in12, in13, in14, in15
  assign imm81 = and_17_out[7:0] | and_18_out[7:0];  // OR_Gate or_9, 8 bits wide
  Multiplexer #(.select(4), .width(3)) multiplexer_9 (
    .in0(Instruction[2:0]), .in1(Instruction[2:0]), .in2(Instruction[2:0]), .in3(Instruction[2:0]),
    .in4(Instruction[2:0]), .in5(Instruction[2:0]), .in6(Instruction[2:0]), .in7(Instruction[10:8]),
    .in8(Instruction[10:8]), .in9(Instruction[10:8]), .in10(Instruction[10:8]), .out(multiplexer_9_out),
    .sel(Code), .en(Enable));  // open: in11, in12, in13, in14, in15

  // Other names for the same wires on the sheet: Imm8[7:0] = Instruction[7:0]; Rd_t[2:0] = Instruction[2:0];
  //   Rm1[2:0] = Instruction[5:3]; Rn_t[2:0] = Instruction[5:3]; Imm3[2:0] = Instruction[8:6];
  //   Imm5_t[4:0] = Instruction[10:6]; Rm2[2:0] = Instruction[8:6]; Rdn[2:0] = Instruction[10:8]

  // Notes on the sheet:
  //   Note: ALU uses Rn register for shifts. Use Rn instead of Rm for shifts (immediate) here too
  //   Note 3: Imm32_Enable forces the use of the immediate for Rm register
  //   Note 3: Imm32_Enable forces the use of the immediate for Rm register
  //   Note: ALU uses Rn register for shifts. Use Rn instead of Rm for shifts (immediate) here too
  //   Note 2: MOV uses RSB ALU opcode with Imm8 reversed so that it is copied to output register
  //   Note 2: MOV uses RSB ALU opcode with Imm8 reversed so that it is copied to output register
  //   Pull output low on Enable = 0
  //   only ADD and SUB use Rm
  //   ALU will use Imm32 instead of Rm
endmodule
