// Logisim project Machine_Logisim3.circ as structural Verilog: 3 circuits, main circuit Facade
module Facade (
);

  wire and_1_out, and_2_out, and_3_out, and_4_out, and_5_out, and_6_out, BREAK, Clk, Clk_Button2,
       Clk_Button_out, clock_1_out, CONTINUE, d_ff_2_qn, decoder_1_out0, decoder_1_out1, decoder_1_out2,
       decoder_1_out3, decoder_1_out4, decoder_1_out5, KEYB_Eof, KEYB_Read, KEYB_ReadEn, MMIO_En, or_1_out,
       or_4_out, Reset, RNG_Read, Rst_Button_out, RST_Signal, Store, TTY_Upd;
  wire [3:0] binary_to_bcd_converter_1_p2, binary_to_bcd_converter_1_p3, binary_to_bcd_converter_1_p4,
       binary_to_bcd_converter_1_p5, CPU_1_flags, MMIO_Addr;
  wire [4:0] JOY_X, JOY_Y;
  wire [6:0] KEYB_Char, TTY_Char;
  wire [7:4] RAM_Addr;
  wire [15:0] multiplier_1_out, ROM_Addr, ROMa_data;
  wire [31:0] bcd8digits_1_bcd, CPU_1_r0, CPU_1_r1, CPU_1_r2, CPU_1_r3, CPU_1_r6, CPU_1_r7, CPU_1_sp, Dip1,
       Dip2, Dip3, divider_1_out, divider_1_rem, MMIO_Out, multiplexer_1_out, R4, R5, RAM_Out, RAMa_dout,
       random_1_out, register_3_q, Res, Screen;
  wire [31:1] undriven_2;
  wire [31:5] undriven_4, undriven_5;
  wire [31:7] undriven, undriven_3;
  wire [31:9] CPU_1_ram_addr;

  DipSwitch dipswitch_1 (
    .sw1(Dip1[7]), .sw2(Dip1[6]), .sw3(Dip1[5]), .sw4(Dip1[4]), .sw5(Dip1[3]), .sw6(Dip1[2]), .sw7(Dip1[1]),
    .sw8(Dip1[0]));
  // Probe on Dip1[7:0]
  DipSwitch dipswitch_2 (
    .sw1(Dip2[7]), .sw2(Dip2[6]), .sw3(Dip2[5]), .sw4(Dip2[4]), .sw5(Dip2[3]), .sw6(Dip2[2]), .sw7(Dip2[1]),
    .sw8(Dip2[0]));
  Keyboard keyboard_1 (.clk(Clk), .re(KEYB_ReadEn), .clr(Reset), .avail(KEYB_Eof), .data(KEYB_Char));
  and and_1 (and_1_out, MMIO_En, Store);
  Decoder #(.select(4)) decoder_1 (
    .out0(decoder_1_out0), .out1(decoder_1_out1), .out2(decoder_1_out2), .out3(decoder_1_out3),
    .out4(decoder_1_out4), .out5(decoder_1_out5), .sel(MMIO_Addr), .en(and_1_out));  // open: out6, out7, out8, out9, out10, out11, out12, out13, out14, out15
  RAM #(.dataWidth(32)) RAMa (
    .addr({RAM_Addr, MMIO_Addr}), .we(and_2_out), .oe(1'b1), .clk(Clk), .din(RAM_Out), .dout(RAMa_dout));
  and and_2 (and_2_out, ~MMIO_En, Store);  // AND_Gate
  // Probe on Dip2[7:0]
  // Probe on MMIO_Addr
  // Probe on {MMIO_En, RAM_Addr, MMIO_Addr}
  // Probe on Dip3[7:0]
  DipSwitch dipswitch_3 (
    .sw1(Dip3[7]), .sw2(Dip3[6]), .sw3(Dip3[5]), .sw4(Dip3[4]), .sw5(Dip3[3]), .sw6(Dip3[2]), .sw7(Dip3[1]),
    .sw8(Dip3[0]));
  Joystick #(.bits(5)) joystick_1 (.x(JOY_X), .y(JOY_Y));
  Register #(.trigger("falling"), .width(7)) register_1 (
    .D(RAM_Out[6:0]), .en(decoder_1_out0), .clk(Clk), .Q(TTY_Char), .clr(Reset));
  Register #(.width(32)) register_2 (.D(RAM_Out), .en(decoder_1_out1), .clk(Clk), .Q(Res), .clr(Reset));
  Register #(.width(32)) register_3 (.D(RAM_Out), .en(decoder_1_out2), .clk(Clk), .Q(register_3_q), .clr(Reset));
  Register #(.width(1)) register_4 (.D(RAM_Out[0]), .en(decoder_1_out4), .clk(Clk), .Q(RST_Signal), .clr(Reset));
  Register #(.width(1)) register_5 (.D(RAM_Out[0]), .en(decoder_1_out5), .clk(Clk), .Q(BREAK), .clr(or_1_out));
  or or_1 (or_1_out, Reset, CONTINUE);
  Clock clock_1 (.out(clock_1_out));
  DotMatrix #(.inputtype("row"), .matrixcols(8), .matrixrows(4)) dotmatrix_1 (
    .row0(Screen[7:0]), .row1(Screen[15:8]), .row2(Screen[23:16]), .row3(Screen[31:24]));
  D_Flip_Flop d_ff_1 (.D(decoder_1_out0), .clk(Clk), .Q(TTY_Upd));  // open: Qn, preset, reset
  Register #(.width(32)) register_6 (.D(register_3_q), .en(and_3_out), .clk(Clk), .Q(Screen), .clr(Reset));
  and and_3 (and_3_out, RAM_Out[0], decoder_1_out3);
  or or_2 (Clk, and_4_out, Clk_Button_out, Clk_Button2);
  and and_4 (and_4_out, clock_1_out, ~BREAK);  // AND_Gate
  Button Clk_Button (.out(Clk_Button_out));
  Button Rst_Button (.out(Rst_Button_out));
  ROM #(.addrWidth(16), .dataWidth(16)) ROMa (.addr(ROM_Addr), .data(ROMa_data));
  or or_3 (Reset, Rst_Button_out, RST_Signal);
  // Probe on RAMa_dout
  Hex_Digit_Display hex_digit_display_1 (.value(Res[15:12]));  // open: dp
  D_Flip_Flop #(.trigger("falling")) d_ff_2 (.D(1'b0), .clk(Clk), .Qn(d_ff_2_qn), .preset(Reset));  // open: Q, reset
  DotMatrix #(.inputtype("row"), .matrixcols(32), .matrixrows(1)) dotmatrix_2 (.row0(Res));
  Hex_Digit_Display hex_digit_display_2 (.value(Res[11:8]));  // open: dp
  Hex_Digit_Display hex_digit_display_3 (.value(Res[7:4]));  // open: dp
  D_Flip_Flop d_ff_3 (.D(KEYB_Read), .clk(Clk), .Q(KEYB_ReadEn), .reset(or_4_out));  // open: Qn, preset
  or or_4 (or_4_out, ~KEYB_Read, Reset);  // OR_Gate
  Multiplexer #(.enable("false"), .width(32)) multiplexer_1 (
    .in0(RAMa_dout), .in1(MMIO_Out), .out(multiplexer_1_out), .sel(MMIO_En));
  // Probe on multiplexer_1_out
  Button button_1 (.out(CONTINUE));
  Hex_Digit_Display hex_digit_display_4 (.value(Res[3:0]));  // open: dp
  // Probe on CPU_1_r1
  // Probe on CPU_1_r0
  and and_5 (and_5_out, Clk, d_ff_2_qn);
  Hex_Digit_Display hex_digit_display_5 (.value(binary_to_bcd_converter_1_p2));  // open: dp
  // Binary_to_BCD_converter #(.binvalue(13)) binary_to_bcd_converter_1: pin names not known; wires that end beside it: Res[12:0], binary_to_bcd_converter_1_p2, binary_to_bcd_converter_1_p3, binary_to_bcd_converter_1_p4, binary_to_bcd_converter_1_p5
  // Probe on CPU_1_r3
  // Probe on CPU_1_r2
  // Probe on R5
  // Probe on R4
  Button button_2 (.out(Clk_Button2));
  // Probe on Res
  Hex_Digit_Display hex_digit_display_6 (.value(binary_to_bcd_converter_1_p3));  // open: dp
  Hex_Digit_Display hex_digit_display_7 (.value(binary_to_bcd_converter_1_p4));  // open: dp
  Random #(.width(32)) random_1 (.next(RNG_Read), .clk(Clk), .out(random_1_out));  // open: clr
  // Probe on CPU_1_r7
  // Probe on CPU_1_r6
  // Probe on CPU_1_flags
  CPU CPU_1 (
    .RAM_Out(RAM_Out), .ROM_Addr(ROM_Addr), .RAM_Addr({CPU_1_ram_addr, MMIO_En, RAM_Addr, MMIO_Addr}),
    .Store(Store), .Flags(CPU_1_flags), .SP(CPU_1_sp), .R0(CPU_1_r0), .R1(CPU_1_r1), .R2(CPU_1_r2),
    .R3(CPU_1_r3), .R4(R4), .R5(R5), .R6(CPU_1_r6), .R7(CPU_1_r7), .RAM_In(multiplexer_1_out),
    .ROM_In(ROMa_data), .Clk(and_5_out), .Reset(Reset));
  Hex_Digit_Display hex_digit_display_8 (.value(binary_to_bcd_converter_1_p5));  // open: dp
  BCD8digits bcd8digits_1 (.BCD(bcd8digits_1_bcd), .Number(Res));
  Divider #(.width(32)) divider_1 (.a(R4), .b(R5), .out(divider_1_out), .rem(divider_1_rem));  // open: upper
  TTY tty_1 (.data(TTY_Char), .clk(Clk), .we(TTY_Upd), .clr(Reset));
  Multiplier #(.width(16)) multiplier_1 (.a(16'h2), .b(ROM_Addr), .out(multiplier_1_out));  // open: cin, cout
  // Probe on {MMIO_En, RAM_Addr, MMIO_Addr}
  // Probe on RAM_Out
  // Probe on CPU_1_sp
  Pull_Resistor pull_resistor_1 (.node(MMIO_Out));
  Multiplexer #(.enable("false"), .select(4), .width(32)) multiplexer_2 (
    .in0({undriven, TTY_Char}), .in1(Res), .in2(register_3_q), .in3(Dip1), .in4(Dip2), .in5(Dip3),
    .in6({undriven_2, KEYB_Eof}), .in7({undriven_3, KEYB_Char}), .in8({undriven_4, JOY_X}),
    .in9({undriven_5, JOY_Y}), .in10(random_1_out), .in11(bcd8digits_1_bcd), .in12(divider_1_out),
    .in13(divider_1_rem), .out(MMIO_Out), .sel(MMIO_Addr));  // open: in14, in15
  // Probe on multiplier_1_out
  and and_6 (and_6_out, ~Store, MMIO_En);  // AND_Gate
  Decoder #(.select(4)) decoder_2 (
    .out7(KEYB_Read), .out10(RNG_Read), .sel(MMIO_Addr), .en(and_6_out));  // open: out0, out1, out2, out3, out4, out5, out6, out8, out9, out11, out12, out13, out14, out15

  // Other names for the same wires on the sheet: RAM_Addr (some bits) = {MMIO_En, MMIO_Addr}

  // Notes on the sheet:
  //   Entrées / Sorties mappées en mémoire
  //   Sorties
  //   contents of ROMa (hex, n*v repeats v):
  //   b0a4 b0ff b0f1 e7fe e7fe 2041 9014 e7fe e7fe 203d 9014 e7fe e7fe 2000 900c e7fe e7fe e7fe 981a 2800
  //   d100 e7fe e7f9 e7fe 981b 900a 980a 900b 980b 280a d100 e7fe e015 980b 2830 db03 e7fe 980b 283a db00
  //   e7fe e7e4 e7fe 980b 9014 e7fe 980c 210a 4341 910c 980b 990c 1808 3830 900c e7d6 980c 9009 9809 900e
  //   e7fe 200a 9014 e7fe e7fe e7fe 2042 9014 e7fe e7fe 203d 9014 e7fe e7fe 2000 9008 e7fe e7fe e7fe 981a
  //   2800 d100 e7fe e7f9 e7fe 981b 9006 9806 9007 9807 280a d100 e7fe e015 9807 2830 db03 e7fe 9807 283a
  //   db00 e7fe e7e4 e7fe 9807 9014 e7fe 9808 210a 4341 9108 9807 9908 1808 3830 9008 e7d6 9808 9005 9805
  //   900d e7fe 200a 9014 9*e7fe 202b 9014 e7fe e7fe 202d 9014 e7fe e7fe e7fe 202a 9014 e7fe e7fe e7fe
  //   202f 9014 e7fe e7fe e7fe 2025 9014 e7fe e7fe e7fe 2026 9014 e7fe e7fe e7fe 207c 9014 e7fe e7fe e7fe
  //   205e 9014 5*e7fe 981a 2800 d100 e7fe e7f9 e7fe 981b 9003 9803 9004 9804 2825 9000 d033 e7fe 9800
  //   2826 d038 e7fe 9800 282a d01d e7fe 9800 282b d00f e7fe 9800 282d d010 e7fe 9800 282f d016 e7fe 9800
  //   285e d02e e7fe 9800 287c d025 e02e 980e 990d 1840 9015 e02a 980e 990d 1a40 9015 e025 980e 990d 4341
  //   9115 e020 980e 990d 4 d 9820 9002 9802 9015 e017 980e 990d 4 d 9821 9001 9801 9015 e00e 980e 990d
  //   4008 9015 e009 980e 990d 4308 9015 e004 980e 990d 4048 9015 e7ff e7a0 e7fe e7fe e7fe 200a 9014 e7fe
  //   e7fe 2052 9014 e7fe e7fe e7fe 203d 9014 e7fe e7fe e7fe 981f 9013 9813 2800 d104 e7fe e7fe 2030 9014
  //   e7fe e033 9815 2800 da09 e7fe e7fe 202d 9014 e7fe 9815 4240 9015 981f 9013 e7fe 2000 9012 9011 e7fe
  //   9811 2807 d81d e7fe 9813 210f 4008 9010 9813 900 9013 9812 2800 d108 e7fe 9810 2800 d002 e7fe 2001
  //   9012 e7ff e005 e7fe e7fe 9810 3030 9014 e7fe e7fe 9811 1c40 9011 e7dc e7fe e7fe e7fe 981a 2800 d100
  //   e7fe e7f9 e7fe e7fe 2001 9018 e7fe e7fd
  //   Reprendre après un point d'arrêt
  //   Tic d'horloge
  //   Entrées
  //   PC effectif
endmodule

module CPU (
  input  [31:0] RAM_In,
  input  [15:0] ROM_In,
  input  Clk,
  input  Reset,
  output [31:0] R3,
  output [31:0] R7,
  output [31:0] R2,
  output [31:0] R6,
  output [31:0] R1,
  output [31:0] R5,
  output [31:0] R0,
  output [31:0] R4,
  output [31:0] RAM_Out,
  output [15:0] ROM_Addr,
  output [31:0] RAM_Addr,
  output Store,
  output [3:0] Flags,
  output [31:0] SP
);

  wire Controller_1_p9, Controller_1_p16, Controller_1_p17, Load;
  wire [2:0] Controller_1_p11, Controller_1_p12, Controller_1_p13;
  wire [3:0] Controller_1_p10, FlagsIn;
  wire [4:0] Controller_1_p15, multiplexer_1_out;
  wire [31:0] DataIn, Imm32, multiplexer_2_out, Regs_1_bout, S;

  // Controller Controller_1: pin names not known; wires that end beside it: ROM_In, Clk, Reset, FlagsIn, ROM_Addr, RAM_Addr, Load, Store, Controller_1_p9, Controller_1_p10, Controller_1_p11, Controller_1_p12, Controller_1_p13, Imm32, Controller_1_p15, Controller_1_p16, Controller_1_p17, Flags, SP
  Multiplexer #(.enable("false"), .width(5)) multiplexer_1 (
    .in0(Controller_1_p15), .in1(RAM_Out[4:0]), .out(multiplexer_1_out), .sel(Controller_1_p16));
  Multiplexer #(.enable("false"), .width(32)) multiplexer_2 (
    .in0(RAM_Out), .in1(Imm32), .out(multiplexer_2_out), .sel(Controller_1_p9));
  ALU ALU_1 (
    .A(multiplexer_2_out), .B(Regs_1_bout), .Shift(multiplexer_1_out), .Codop(Controller_1_p10),
    .CarryIn(Controller_1_p17), .S(S), .Flags(FlagsIn));
  BancRegistre Regs_1 (
    .AOut(RAM_Out), .BOut(Regs_1_bout), .R7(R7), .R0(R0), .R1(R1), .R2(R2), .R3(R3), .R4(R4), .R5(R5),
    .R6(R6), .DataIn(DataIn), .RegDest(Controller_1_p11), .Clk(Clk), .Reset(Reset), .RegA(Controller_1_p12),
    .RegB(Controller_1_p13));
  Multiplexer #(.enable("false"), .width(32)) multiplexer_3 (.in0(S), .in1(RAM_In), .out(DataIn), .sel(Load));

  // Other names for the same wires on the sheet: AOut[31:0] = RAM_Out
endmodule

module BCD8digits (
  input  [31:0] Number,
  output [31:0] BCD
);

  wire [31:0] divider_1_out, divider_2_out, divider_3_out, divider_4_out, divider_5_out, divider_6_out,
       divider_7_out;
  wire [31:4] divider_1_rem, divider_2_rem, divider_3_rem, divider_4_rem, divider_5_rem, divider_6_rem,
       divider_7_rem, divider_8_rem;

  Divider #(.width(32)) divider_1 (
    .a(Number), .b(32'ha), .out(divider_1_out), .rem({divider_1_rem, BCD[31:28]}));  // open: upper
  Divider #(.width(32)) divider_2 (
    .a(divider_1_out), .b(32'ha), .out(divider_2_out), .rem({divider_2_rem, BCD[27:24]}));  // open: upper
  Divider #(.width(32)) divider_3 (
    .a(divider_2_out), .b(32'ha), .out(divider_3_out), .rem({divider_3_rem, BCD[23:20]}));  // open: upper
  Divider #(.width(32)) divider_4 (
    .a(divider_3_out), .b(32'ha), .out(divider_4_out), .rem({divider_4_rem, BCD[19:16]}));  // open: upper
  Divider #(.width(32)) divider_5 (
    .a(divider_4_out), .b(32'ha), .out(divider_5_out), .rem({divider_5_rem, BCD[15:12]}));  // open: upper
  Divider #(.width(32)) divider_6 (
    .a(divider_5_out), .b(32'ha), .out(divider_6_out), .rem({divider_6_rem, BCD[11:8]}));  // open: upper
  Divider #(.width(32)) divider_7 (
    .a(divider_6_out), .b(32'ha), .out(divider_7_out), .rem({divider_7_rem, BCD[7:4]}));  // open: upper
  Divider #(.width(32)) divider_8 (.a(divider_7_out), .b(32'ha), .rem({divider_8_rem, BCD[3:0]}));  // open: out, upper
  // Probe on BCD
endmodule
